// Logisim project 8-bitCPU.circ as structural Verilog: 40 circuits, main circuit main
module main (
);


  // Notes on the sheet:
  //   CpE 402 / 402L - Computer Architecture and Organization
  //   Final Project
  //   8-BIT CPU DESIGN AND IMPLEMENTATION USING LOGISIM & VERILOG
  //   Submitted by:
  //   BSCpE 4A - GROUP 2
  //   ARMADO, James Neftali B.
  //   ANDAL, Anthony Aries C.
  //   BINOSA, Joyce C.
  //   BUENAVENTURA, Ralph D.
  //   CAPARAS, Mumphry S.
  //   CARASIG, Janelle Isabel M.
  //   CASTRO, Ia Micah G.
  //   CERRO, Christian Paul
  //   CORREA, Reingel F.
  //   DELA CRUZ, Jay Vee A.
  //   ERFE, Irysse J.
  //   LORENZO, Yesuah Jirah D.
  //   Submitted to:
  //   Engr. Alberto C. Cruz Jr., PCpE
  //   Instructor
endmodule

module CPU_MEM_1 (
  input  e,
  input  s,
  output q
);

  D_Flip_Flop #(.trigger("high")) d_ff_1 (.clk(e), .D(s), .Q(q));  // open: Qn, preset, reset
endmodule

module CPU_MEM_8 (
  input  [7:0] i,
  input  e,
  output [7:0] o
);

  CPU_MEM_1 cpu_mem_1_1 (.e(e), .s(i[0]), .q(o[0]));
  CPU_MEM_1 cpu_mem_1_2 (.e(e), .s(i[1]), .q(o[1]));
  CPU_MEM_1 cpu_mem_1_3 (.e(e), .s(i[2]), .q(o[2]));
  CPU_MEM_1 cpu_mem_1_4 (.e(e), .s(i[3]), .q(o[3]));
  CPU_MEM_1 cpu_mem_1_5 (.e(e), .s(i[4]), .q(o[4]));
  CPU_MEM_1 cpu_mem_1_6 (.e(e), .s(i[5]), .q(o[5]));
  CPU_MEM_1 cpu_mem_1_7 (.e(e), .s(i[6]), .q(o[6]));
  CPU_MEM_1 cpu_mem_1_8 (.e(e), .s(i[7]), .q(o[7]));
endmodule

module CPU_ENABLE (
  input  [7:0] i,
  input  e,
  output [7:0] o
);

  and and_1 (o[0], i[0], e);
  and and_2 (o[1], i[1], e);
  and and_3 (o[2], i[2], e);
  and and_4 (o[3], i[3], e);
  and and_5 (o[4], i[4], e);
  and and_6 (o[5], i[5], e);
  and and_7 (o[6], i[6], e);
  and and_8 (o[7], i[7], e);
endmodule

module CPU_REG_8 (
  input  [7:0] i,
  input  s,
  input  e,
  output [7:0] REG,
  output [7:0] o
);

  wire [7:0] cpu_enable_1_o;

  CPU_MEM_8 cpu_mem_8_1 (.o(REG), .i(i), .e(s));
  CPU_ENABLE cpu_enable_1 (.i(REG), .e(e), .o(cpu_enable_1_o));
  assign o = e ? cpu_enable_1_o : 8'bz;  // Controlled_Buffer controlled_buffer_1
endmodule

module CPU_R (
  input  [7:0] i,
  input  s,
  input  e,
  output [7:0] \reg ,
  output [7:0] o
);

  CPU_REG_8 cpu_reg_8_1 (.i(i), .s(s), .e(e), .REG(\reg ), .o(o));
endmodule

module CPU_TMP (
  input  [7:0] i,
  input  in_2,
  output [7:0] o
);

  wire [7:0] controlled_buffer_1_out;

  assign controlled_buffer_1_out = in_2 ? i : 8'bz;  // Controlled_Buffer controlled_buffer_1
  CPU_MEM_8 cpu_mem_8_1 (.o(o), .i(controlled_buffer_1_out), .e(in_2));
endmodule

module CPU_ACCUMULATOR (
  input  [7:0] i,
  input  s,
  input  e,
  output [7:0] \reg ,
  output [7:0] o
);

  CPU_REG_8 cpu_reg_8_1 (.i(i), .s(s), .e(e), .REG(\reg ), .o(o));
endmodule

module CPU_IAR (
  input  [7:0] i,
  input  s,
  input  e,
  output [7:0] IAR,
  output [7:0] o
);

  CPU_REG_8 cpu_reg_8_1 (.i(i), .s(s), .e(e), .REG(IAR), .o(o));
endmodule

module CPU_IR (
  input  [7:0] i,
  input  s,
  output [7:0] o
);

  CPU_MEM_8 cpu_mem_8_1 (.o(o), .i(i), .e(s));
endmodule

module CPU_FLAGS (
  input  C,
  input  A,
  input  E,
  input  Z,
  input  s,
  output C_2,
  output A_2,
  output E_2,
  output Z_2
);

  CPU_MEM_1 cpu_mem_1_1 (.e(s), .s(C), .q(C_2));
  CPU_MEM_1 cpu_mem_1_2 (.e(s), .s(A), .q(A_2));
  CPU_MEM_1 cpu_mem_1_3 (.e(s), .s(E), .q(E_2));
  CPU_MEM_1 cpu_mem_1_4 (.e(s), .s(Z), .q(Z_2));
endmodule

module CPU_ADDER (
  input  a,
  input  b,
  input  Cin,
  output sum,
  output Cout
);

  wire and_1_out, and_2_out, xor_1_out;

  xor xor_1 (xor_1_out, a, b);
  xor xor_2 (sum, xor_1_out, Cin);
  and and_1 (and_1_out, Cin, xor_1_out);
  and and_2 (and_2_out, a, b);
  or or_1 (Cout, and_1_out, and_2_out);
endmodule

module CPU_ADDER_8 (
  input  [7:0] a,
  input  cin,
  input  [7:0] b,
  output cout,
  output [7:0] sum
);

  wire cpu_adder_2_cout, cpu_adder_3_cout, cpu_adder_4_cout, cpu_adder_5_cout, cpu_adder_6_cout,
       cpu_adder_7_cout, cpu_adder_8_cout;

  CPU_ADDER cpu_adder_1 (.a(a[7]), .b(b[7]), .Cin(cpu_adder_2_cout), .sum(sum[7]), .Cout(cout));
  CPU_ADDER cpu_adder_2 (.a(a[6]), .b(b[6]), .Cin(cpu_adder_3_cout), .sum(sum[6]), .Cout(cpu_adder_2_cout));
  CPU_ADDER cpu_adder_3 (.a(a[5]), .b(b[5]), .Cin(cpu_adder_4_cout), .sum(sum[5]), .Cout(cpu_adder_3_cout));
  CPU_ADDER cpu_adder_4 (.a(a[4]), .b(b[4]), .Cin(cpu_adder_5_cout), .sum(sum[4]), .Cout(cpu_adder_4_cout));
  CPU_ADDER cpu_adder_5 (.a(a[3]), .b(b[3]), .Cin(cpu_adder_6_cout), .sum(sum[3]), .Cout(cpu_adder_5_cout));
  CPU_ADDER cpu_adder_6 (.a(a[2]), .b(b[2]), .Cin(cpu_adder_7_cout), .sum(sum[2]), .Cout(cpu_adder_6_cout));
  CPU_ADDER cpu_adder_7 (.a(a[1]), .b(b[1]), .Cin(cpu_adder_8_cout), .sum(sum[1]), .Cout(cpu_adder_7_cout));
  CPU_ADDER cpu_adder_8 (.a(a[0]), .b(b[0]), .Cin(cin), .sum(sum[0]), .Cout(cpu_adder_8_cout));
endmodule

module CPU_NOT (
  input  [7:0] i,
  output [7:0] o
);

  not not_1 (o[0], i[0]);
  not not_2 (o[1], i[1]);
  not not_3 (o[2], i[2]);
  not not_4 (o[3], i[3]);
  not not_5 (o[4], i[4]);
  not not_6 (o[5], i[5]);
  not not_7 (o[6], i[6]);
  not not_8 (o[7], i[7]);
endmodule

module CPU_AND (
  input  [7:0] a,
  input  [7:0] b,
  output [7:0] o
);

  and and_1 (o[0], a[0], b[0]);
  and and_2 (o[1], a[1], b[1]);
  and and_3 (o[2], a[2], b[2]);
  and and_4 (o[3], a[3], b[3]);
  and and_5 (o[4], a[4], b[4]);
  and and_6 (o[5], a[5], b[5]);
  and and_7 (o[6], a[6], b[6]);
  and and_8 (o[7], a[7], b[7]);
endmodule

module CPU_OR (
  input  [7:0] a,
  input  [7:0] b,
  output [7:0] o
);

  or or_1 (o[0], a[0], b[0]);
  or or_2 (o[1], a[1], b[1]);
  or or_3 (o[2], a[2], b[2]);
  or or_4 (o[3], a[3], b[3]);
  or or_5 (o[4], a[4], b[4]);
  or or_6 (o[5], a[5], b[5]);
  or or_7 (o[6], a[6], b[6]);
  or or_8 (o[7], a[7], b[7]);
endmodule

module CPU_XOR_LE (
  input  above_equal,
  input  a_larger,
  input  a,
  input  b,
  output c,
  output equal,
  output a_large
);

  wire and_2_out, not_1_out;

  xor xor_1 (c, a, b);
  not not_1 (not_1_out, c);
  and and_1 (equal, not_1_out, above_equal);
  and and_2 (and_2_out, a, above_equal, c);
  or or_1 (a_large, and_2_out, a_larger);
endmodule

module CPU_XOR_LE_8 (
  input  [7:0] a,
  input  [7:0] b,
  output [7:0] o,
  output larger,
  output equal
);

  wire cpu_xor_le_1_a_large, cpu_xor_le_1_equal, cpu_xor_le_2_a_large, cpu_xor_le_2_equal,
       cpu_xor_le_3_a_large, cpu_xor_le_3_equal, cpu_xor_le_4_a_large, cpu_xor_le_4_equal,
       cpu_xor_le_5_a_large, cpu_xor_le_5_equal, cpu_xor_le_6_a_large, cpu_xor_le_6_equal,
       cpu_xor_le_7_a_large, cpu_xor_le_7_equal;

  CPU_XOR_LE cpu_xor_le_1 (
    .a(a[0]), .b(b[0]), .c(o[0]), .above_equal(1'b1), .a_larger(1'b0), .equal(cpu_xor_le_1_equal),
    .a_large(cpu_xor_le_1_a_large));
  CPU_XOR_LE cpu_xor_le_2 (
    .a(a[1]), .b(b[1]), .c(o[1]), .above_equal(cpu_xor_le_1_equal), .a_larger(cpu_xor_le_1_a_large),
    .equal(cpu_xor_le_2_equal), .a_large(cpu_xor_le_2_a_large));
  CPU_XOR_LE cpu_xor_le_3 (
    .a(a[2]), .b(b[2]), .c(o[2]), .above_equal(cpu_xor_le_2_equal), .a_larger(cpu_xor_le_2_a_large),
    .equal(cpu_xor_le_3_equal), .a_large(cpu_xor_le_3_a_large));
  CPU_XOR_LE cpu_xor_le_4 (
    .a(a[3]), .b(b[3]), .c(o[3]), .above_equal(cpu_xor_le_3_equal), .a_larger(cpu_xor_le_3_a_large),
    .equal(cpu_xor_le_4_equal), .a_large(cpu_xor_le_4_a_large));
  CPU_XOR_LE cpu_xor_le_5 (
    .a(a[4]), .b(b[4]), .c(o[4]), .above_equal(cpu_xor_le_4_equal), .a_larger(cpu_xor_le_4_a_large),
    .equal(cpu_xor_le_5_equal), .a_large(cpu_xor_le_5_a_large));
  CPU_XOR_LE cpu_xor_le_6 (
    .a(a[5]), .b(b[5]), .c(o[5]), .above_equal(cpu_xor_le_5_equal), .a_larger(cpu_xor_le_5_a_large),
    .equal(cpu_xor_le_6_equal), .a_large(cpu_xor_le_6_a_large));
  CPU_XOR_LE cpu_xor_le_7 (
    .a(a[6]), .b(b[6]), .c(o[6]), .above_equal(cpu_xor_le_6_equal), .a_larger(cpu_xor_le_6_a_large),
    .equal(cpu_xor_le_7_equal), .a_large(cpu_xor_le_7_a_large));
  CPU_XOR_LE cpu_xor_le_8 (
    .a(a[7]), .b(b[7]), .c(o[7]), .above_equal(cpu_xor_le_7_equal), .a_larger(cpu_xor_le_7_a_large),
    .equal(equal), .a_large(larger));
endmodule

module CPU_SHR (
  input  shift_in,
  input  [7:0] i,
  output [7:0] o,
  output shift_out
);

  wire [7:1] cpu_reg_8_1_o;

  CPU_REG_8 cpu_reg_8_1 (.i(i), .s(1'b1), .e(1'b1), .o({cpu_reg_8_1_o, shift_out}));  // open: REG
  CPU_REG_8 cpu_reg_8_2 (.i({shift_in, cpu_reg_8_1_o}), .s(1'b1), .e(1'b1), .o(o));  // open: REG
endmodule

module CPU_SHL (
  input  shift_in,
  input  [7:0] i,
  output [7:0] o,
  output shift_out
);

  wire [6:0] cpu_reg_8_1_o;

  CPU_REG_8 cpu_reg_8_1 (.i(i), .s(1'b1), .e(1'b1), .o({shift_out, cpu_reg_8_1_o}));  // open: REG
  CPU_REG_8 cpu_reg_8_2 (.i({cpu_reg_8_1_o, shift_in}), .s(1'b1), .e(1'b1), .o(o));  // open: REG
endmodule

module CPU_DECODER_3x8 (
  input  c,
  input  b,
  input  a,
  output [7:0] o
);

  wire not_1_out, not_2_out, not_3_out;

  not not_1 (not_1_out, c);
  not not_2 (not_2_out, b);
  not not_3 (not_3_out, a);
  and and_1 (o[0], not_3_out, not_2_out, not_1_out);
  and and_2 (o[1], a, not_2_out, not_1_out);
  and and_3 (o[2], not_3_out, b, not_1_out);
  and and_4 (o[3], a, b, not_1_out);
  and and_5 (o[4], not_3_out, not_2_out, c);
  and and_6 (o[5], a, not_2_out, c);
  and and_7 (o[6], not_3_out, b, c);
  and and_8 (o[7], a, b, c);

  // Notes on the sheet:
  //   msb
  //   lsb
endmodule

module CPU_E (
  input  [7:0] a,
  input  e,
  output [7:0] o
);

  wire and_1_out, and_2_out, and_3_out, and_4_out, and_5_out, and_6_out, and_7_out, and_8_out;

  assign o[0] = e ? and_1_out : 1'bz;  // Controlled_Buffer controlled_buffer_1
  and and_1 (and_1_out, a[0], e);
  and and_2 (and_2_out, a[1], e);
  assign o[1] = e ? and_2_out : 1'bz;  // Controlled_Buffer controlled_buffer_2
  and and_3 (and_3_out, a[2], e);
  assign o[2] = e ? and_3_out : 1'bz;  // Controlled_Buffer controlled_buffer_3
  and and_4 (and_4_out, a[3], e);
  assign o[3] = e ? and_4_out : 1'bz;  // Controlled_Buffer controlled_buffer_4
  assign o[4] = e ? and_5_out : 1'bz;  // Controlled_Buffer controlled_buffer_5
  and and_5 (and_5_out, a[4], e);
  assign o[5] = e ? and_6_out : 1'bz;  // Controlled_Buffer controlled_buffer_6
  and and_6 (and_6_out, a[5], e);
  and and_7 (and_7_out, a[6], e);
  assign o[6] = e ? and_7_out : 1'bz;  // Controlled_Buffer controlled_buffer_7
  assign o[7] = e ? and_8_out : 1'bz;  // Controlled_Buffer controlled_buffer_8
  and and_8 (and_8_out, a[7], e);
endmodule

module CPU_Z (
  input  [7:0] i,
  output o
);

  wire or_1_out;

  or or_1 (or_1_out, i[0], i[1], i[2], i[3], i[4], i[5], i[6], i[7]);
  not not_1 (o, or_1_out);
endmodule

module CPU_ALU (
  input  [7:0] a,
  input  [7:0] b,
  input  carry_in,
  input  a_2,
  input  b_2,
  input  c,
  output a_larger,
  output equal,
  output zero,
  output [7:0] o,
  output carry_out
);

  wire and_1_out, and_2_out, and_3_out, cpu_adder_8_1_cout, cpu_shl_1_shift_out, cpu_shr_1_shift_out;
  wire [7:0] cpu_adder_8_1_sum, cpu_and_1_o, cpu_decoder_3x8_1_o, cpu_not_1_o, cpu_or_1_o, cpu_shl_1_o,
       cpu_shr_1_o, cpu_xor_le_8_1_o;

  CPU_XOR_LE_8 cpu_xor_le_8_1 (.a(a), .b(b), .o(cpu_xor_le_8_1_o), .larger(a_larger), .equal(equal));
  CPU_OR cpu_or_1 (.a(a), .b(b), .o(cpu_or_1_o));
  CPU_AND cpu_and_1 (.a(a), .b(b), .o(cpu_and_1_o));
  CPU_NOT cpu_not_1 (.i(a), .o(cpu_not_1_o));
  CPU_SHL cpu_shl_1 (.i(a), .shift_out(cpu_shl_1_shift_out), .shift_in(carry_in), .o(cpu_shl_1_o));
  CPU_SHR cpu_shr_1 (.shift_out(cpu_shr_1_shift_out), .i(a), .o(cpu_shr_1_o), .shift_in(carry_in));
  CPU_ADDER_8 cpu_adder_8_1 (.a(a), .cin(carry_in), .b(b), .cout(cpu_adder_8_1_cout), .sum(cpu_adder_8_1_sum));
  CPU_DECODER_3x8 cpu_decoder_3x8_1 (.o(cpu_decoder_3x8_1_o), .c(c), .b(b_2), .a(a_2));
  CPU_E cpu_e_1 (.a(cpu_xor_le_8_1_o), .e(cpu_decoder_3x8_1_o[6]), .o(o));
  CPU_E cpu_e_2 (.a(cpu_or_1_o), .e(cpu_decoder_3x8_1_o[5]), .o(o));
  CPU_E cpu_e_3 (.a(cpu_and_1_o), .e(cpu_decoder_3x8_1_o[4]), .o(o));
  CPU_E cpu_e_4 (.a(cpu_not_1_o), .e(cpu_decoder_3x8_1_o[3]), .o(o));
  CPU_E cpu_e_5 (.a(cpu_shl_1_o), .e(cpu_decoder_3x8_1_o[2]), .o(o));
  CPU_E cpu_e_6 (.a(cpu_shr_1_o), .e(cpu_decoder_3x8_1_o[1]), .o(o));
  CPU_E cpu_e_7 (.a(cpu_adder_8_1_sum), .e(cpu_decoder_3x8_1_o[0]), .o(o));
  and and_1 (and_1_out, cpu_shl_1_shift_out, cpu_decoder_3x8_1_o[2]);
  assign carry_out = cpu_decoder_3x8_1_o[2] ? and_1_out : 1'bz;  // Controlled_Buffer controlled_buffer_1
  assign carry_out = cpu_decoder_3x8_1_o[1] ? and_2_out : 1'bz;  // Controlled_Buffer controlled_buffer_2
  and and_2 (and_2_out, cpu_shr_1_shift_out, cpu_decoder_3x8_1_o[1]);
  and and_3 (and_3_out, cpu_adder_8_1_cout, cpu_decoder_3x8_1_o[0]);
  assign carry_out = cpu_decoder_3x8_1_o[0] ? and_3_out : 1'bz;  // Controlled_Buffer controlled_buffer_3
  CPU_Z cpu_z_1 (.i(o), .o(zero));

  // Notes on the sheet:
  //   b: pull=down
  //   a: pull=down
endmodule

module SAP_1_CONTROL_UNIT (
  input  i7,
  input  i6,
  input  i5,
  input  i4,
  input  CLR,
  output Cp,
  output Ep,
  output Lm,
  output CE,
  output Li,
  output Ei,
  output LA,
  output EA,
  output Su,
  output Eu,
  output LB,
  output Lo
);

  wire and_1_out, and_2_out, and_3_out, and_4_out, and_5_out, and_6_out, and_7_out, and_8_out, and_9_out,
       and_10_out, and_11_out, and_13_out, and_15_out, and_16_out, and_17_out, and_18_out, C32_2_out,
       C32_out, C33_2_out, C33_out, C34_out, CLK_out, d_ff_1_q, d_ff_2_q, d_ff_3_q, d_ff_4_q, not_1_out,
       not_2_out, not_3_out, not_4_out, or_1_out, or_2_out, or_3_out, or_4_out, or_6_out;

  not not_1 (not_1_out, i7);
  not not_2 (not_2_out, i6);
  not not_3 (not_3_out, i5);
  not not_4 (not_4_out, i4);
  and C32 (C32_out, not_1_out, not_2_out, not_3_out, not_4_out);
  and C32_2 (C32_2_out, not_1_out, not_2_out, not_3_out, i4);
  and C33 (C33_out, not_1_out, not_2_out, i5, not_4_out);
  and C33_2 (C33_2_out, i7, i6, i5, not_4_out);
  nand C34 (C34_out, i7, i6, i5, i4);
  D_Flip_Flop d_ff_1 (.clk(CLK_out), .D(d_ff_2_q), .Q(d_ff_1_q), .reset(CLR));  // open: Qn, preset
  and and_1 (and_1_out, C32_2_out, d_ff_3_q);
  and and_2 (and_2_out, C32_out, d_ff_3_q);
  or or_1 (or_1_out, Ep, and_2_out, and_1_out, and_3_out);
  not not_5 (Lm, or_1_out);
  and and_3 (and_3_out, C33_out, d_ff_3_q);
  D_Flip_Flop d_ff_2 (.clk(CLK_out), .D(d_ff_3_q), .Q(d_ff_2_q), .reset(CLR));  // open: Qn, preset
  and and_4 (and_4_out, C32_2_out, d_ff_2_q);
  and and_5 (and_5_out, C32_out, d_ff_2_q);
  or or_2 (or_2_out, d_ff_4_q, and_5_out, and_4_out, and_6_out);
  not not_6 (CE, or_2_out);
  and and_6 (and_6_out, C33_out, d_ff_2_q);
  not not_7 (Li, d_ff_4_q);
  D_Flip_Flop d_ff_3 (.clk(CLK_out), .D(d_ff_4_q), .Q(d_ff_3_q), .reset(CLR));  // open: Qn, preset
  and and_7 (and_7_out, C32_out, d_ff_3_q);
  and and_8 (and_8_out, C32_2_out, d_ff_3_q);
  or or_3 (or_3_out, and_7_out, and_8_out, and_9_out);
  not not_8 (Ei, or_3_out);
  D_Flip_Flop d_ff_4 (.clk(CLK_out), .D(Cp), .Q(d_ff_4_q), .reset(CLR));  // open: Qn, preset
  and and_9 (and_9_out, C33_out, d_ff_3_q);
  and and_10 (and_10_out, C32_out, d_ff_2_q);
  and and_11 (and_11_out, C32_2_out, d_ff_1_q);
  or or_4 (or_4_out, and_10_out, and_11_out, and_13_out);
  not not_9 (LA, or_4_out);
  D_Flip_Flop d_ff_5 (.clk(CLK_out), .D(Ep), .Q(Cp), .reset(CLR));  // open: Qn, preset
  and and_12 (EA, C33_2_out, d_ff_3_q);
  and and_13 (and_13_out, C33_out, d_ff_1_q);
  and and_14 (Su, C33_out, d_ff_1_q);
  and and_15 (and_15_out, C32_2_out, d_ff_1_q);
  Clock CLK (.out(CLK_out));
  D_Flip_Flop d_ff_6 (.clk(CLK_out), .D(d_ff_1_q), .Q(Ep), .preset(CLR));  // open: Qn, reset
  and and_16 (and_16_out, C33_out, d_ff_1_q);
  or or_5 (Eu, and_15_out, and_16_out);
  and and_17 (and_17_out, C32_2_out, d_ff_2_q);
  and and_18 (and_18_out, C33_out, d_ff_2_q);
  or or_6 (or_6_out, and_17_out, and_18_out);
  not not_10 (LB, or_6_out);
  nand nand_1 (Lo, C33_2_out, d_ff_3_q);

  // Notes on the sheet:
  //   INSTRUCTION$    DECODER
  //   LDA
  //   ADD
  //   SUB
  //   OUT
  //   HLT
  //   T6
  //   T5
  //   RING COUNTER
  //   T4
  //   CONTROL MATRIX
  //   T3
  //   T2
  //   T1
  //   C43
endmodule

module CPU_CLK (
  input  clkin,
  output clk,
  output clks,
  output clke
);

  wire j_k_ff_1_qn, nand_1_out;

  J_K_Flip_Flop #(.Pre_Clr_Positions("LEGACY"), .enable("true")) j_k_ff_1 (
    .J(1'b1), .clk(clkin), .K(1'b1), .Q(clk), .Qn(j_k_ff_1_qn));  // open: preset, en, reset
  nand nand_1 (nand_1_out, clkin, clk);
  nand nand_2 (clke, j_k_ff_1_qn, clkin);
  not not_1 (clks, nand_1_out);
endmodule

module CPU_STEPPER (
  input  reset,
  input  clk,
  output step_1,
  output step_2,
  output step_3,
  output step_4,
  output step_5,
  output step_6,
  output step_7
);

  wire cpu_mem_1_1_q, cpu_mem_1_2_q, cpu_mem_1_3_q, cpu_mem_1_4_q, cpu_mem_1_5_q, cpu_mem_1_6_q,
       cpu_mem_1_7_q, cpu_mem_1_8_q, cpu_mem_1_9_q, cpu_mem_1_10_q, cpu_mem_1_11_q, not_1_out, not_2_out,
       not_3_out, not_4_out, not_5_out, not_6_out, not_7_out, not_8_out, or_1_out, or_2_out;

  not not_1 (not_1_out, clk);
  not not_2 (not_2_out, reset);
  or or_1 (or_1_out, reset, clk);
  or or_2 (or_2_out, reset, not_1_out);
  or or_3 (step_1, reset, not_3_out);
  CPU_MEM_1 cpu_mem_1_1 (.e(or_1_out), .s(not_2_out), .q(cpu_mem_1_1_q));
  not not_3 (not_3_out, cpu_mem_1_2_q);
  CPU_MEM_1 cpu_mem_1_2 (.e(or_2_out), .s(cpu_mem_1_1_q), .q(cpu_mem_1_2_q));
  and and_1 (step_2, cpu_mem_1_2_q, not_4_out);
  CPU_MEM_1 cpu_mem_1_3 (.e(or_1_out), .s(cpu_mem_1_2_q), .q(cpu_mem_1_3_q));
  not not_4 (not_4_out, cpu_mem_1_4_q);
  CPU_MEM_1 cpu_mem_1_4 (.e(or_2_out), .s(cpu_mem_1_3_q), .q(cpu_mem_1_4_q));
  and and_2 (step_3, cpu_mem_1_4_q, not_5_out);
  CPU_MEM_1 cpu_mem_1_5 (.e(or_1_out), .s(cpu_mem_1_4_q), .q(cpu_mem_1_5_q));
  not not_5 (not_5_out, cpu_mem_1_6_q);
  and and_3 (step_4, cpu_mem_1_6_q, not_6_out);
  CPU_MEM_1 cpu_mem_1_6 (.e(or_2_out), .s(cpu_mem_1_5_q), .q(cpu_mem_1_6_q));
  CPU_MEM_1 cpu_mem_1_7 (.e(or_1_out), .s(cpu_mem_1_6_q), .q(cpu_mem_1_7_q));
  and and_4 (step_5, cpu_mem_1_8_q, not_7_out);
  not not_6 (not_6_out, cpu_mem_1_8_q);
  CPU_MEM_1 cpu_mem_1_8 (.e(or_2_out), .s(cpu_mem_1_7_q), .q(cpu_mem_1_8_q));
  CPU_MEM_1 cpu_mem_1_9 (.e(or_1_out), .s(cpu_mem_1_8_q), .q(cpu_mem_1_9_q));
  not not_7 (not_7_out, cpu_mem_1_10_q);
  CPU_MEM_1 cpu_mem_1_10 (.e(or_2_out), .s(cpu_mem_1_9_q), .q(cpu_mem_1_10_q));
  and and_5 (step_6, cpu_mem_1_10_q, not_8_out);
  not not_8 (not_8_out, step_7);
  CPU_MEM_1 cpu_mem_1_11 (.e(or_1_out), .s(cpu_mem_1_10_q), .q(cpu_mem_1_11_q));
  CPU_MEM_1 cpu_mem_1_12 (.e(or_2_out), .s(cpu_mem_1_11_q), .q(step_7));
endmodule

module CPU_DECODER_2x4 (
  input  a,
  input  b,
  output _0,
  output _1,
  output _2,
  output _3
);

  wire not_1_out, not_2_out;

  not not_1 (not_1_out, a);
  not not_2 (not_2_out, b);
  and and_1 (_0, not_1_out, not_2_out);
  and and_2 (_1, not_2_out, a);
  and and_3 (_2, not_1_out, b);
  and and_4 (_3, b, a);
endmodule

module CPU_DECODER_2x4_WEST (
  input  a,
  input  b,
  output _0,
  output _1,
  output _2,
  output _3
);

  wire not_1_out, not_2_out;

  not not_1 (not_1_out, a);
  not not_2 (not_2_out, b);
  and and_1 (_0, not_1_out, not_2_out);
  and and_2 (_1, not_2_out, a);
  and and_3 (_2, not_1_out, b);
  and and_4 (_3, b, a);
endmodule

module CPU_DECODER_CTRL_3x8 (
  input  c,
  input  b,
  input  a,
  output _0,
  output _1,
  output _2,
  output _3,
  output _4,
  output _5,
  output _6,
  output _7
);

  wire not_1_out, not_2_out, not_3_out;

  not not_1 (not_1_out, c);
  not not_2 (not_2_out, b);
  not not_3 (not_3_out, a);
  and and_1 (_0, not_3_out, not_2_out, not_1_out);
  and and_2 (_1, a, not_2_out, not_1_out);
  and and_3 (_2, not_3_out, b, not_1_out);
  and and_4 (_3, a, b, not_1_out);
  and and_5 (_4, not_3_out, not_2_out, c);
  and and_6 (_5, a, not_2_out, c);
  and and_7 (_6, not_3_out, b, c);
  and and_8 (_7, a, b, c);
endmodule

module CPU_CONTROL_SECTION (
  input  clks,
  input  clk,
  input  clke,
  input  LOAD,
  input  in_5,
  input  MARS,
  input  C,
  input  A,
  input  E,
  input  Z,
  input  [7:0] IR_IN,
  output BUS_1,
  output IR_S,
  output MAR_S,
  output IAR_E,
  output IAR_S,
  output RAM_E,
  output ACC_S,
  output ACC_E,
  output RAM_S,
  output C_2,
  output TMP_S,
  output IO_CLK_E,
  output FLAG_S,
  output IO_CLK_S,
  output R0_S,
  output R1_S,
  output R0_E,
  output R1_E,
  output R2_S,
  output R2_E,
  output R3_E,
  output R3_S,
  output END,
  output IO,
  output DA,
  output ALU_0,
  output ALU_1,
  output ALU_2
);

  wire and_5_out, and_6_out, and_7_out, and_8_out, and_9_out, and_10_out, and_11_out, and_12_out, and_16_out,
       and_17_out, and_18_out, and_19_out, and_20_out, and_21_out, and_22_out, and_23_out, and_24_out,
       and_25_out, and_26_out, and_27_out, and_28_out, and_29_out, and_30_out, and_31_out, and_32_out,
       and_33_out, and_34_out, and_35_out, and_36_out, and_37_out, and_38_out, and_39_out, and_42_out,
       and_43_out, and_44_out, and_45_out, and_46_out, and_47_out, and_48_out, and_49_out, and_50_out,
       and_51_out, and_52_out, and_53_out, and_54_out, and_55_out, and_56_out, and_57_out, and_58_out,
       and_60_out, and_61_out, and_62_out, and_63_out, cpu_decoder_2x4_1__0, cpu_decoder_2x4_1__1,
       cpu_decoder_2x4_1__2, cpu_decoder_2x4_1__3, cpu_decoder_2x4_west_1__0, cpu_decoder_2x4_west_1__1,
       cpu_decoder_2x4_west_1__2, cpu_decoder_2x4_west_1__3, cpu_decoder_2x4_west_2__0,
       cpu_decoder_2x4_west_2__1, cpu_decoder_2x4_west_2__2, cpu_decoder_2x4_west_2__3,
       cpu_decoder_ctrl_3x8_1__0, cpu_decoder_ctrl_3x8_1__1, cpu_decoder_ctrl_3x8_1__2,
       cpu_decoder_ctrl_3x8_1__3, cpu_decoder_ctrl_3x8_1__4, cpu_decoder_ctrl_3x8_1__5,
       cpu_decoder_ctrl_3x8_1__6, cpu_decoder_ctrl_3x8_1__7, cpu_stepper_1_step_1, cpu_stepper_1_step_2,
       cpu_stepper_1_step_3, cpu_stepper_1_step_4, cpu_stepper_1_step_5, cpu_stepper_1_step_6,
       cpu_stepper_1_step_7, not_1_out, not_2_out, not_3_out, not_4_out, not_5_out, not_6_out, not_7_out,
       or_6_out, or_7_out, or_8_out, or_9_out, or_10_out, or_11_out, or_12_out, or_13_out, or_14_out,
       or_15_out, or_16_out, or_17_out;

  and and_1 (IAR_E, clke, or_6_out);
  and and_2 (RAM_E, clke, or_7_out);
  and and_3 (ACC_E, clke, or_8_out);
  and and_4 (IO_CLK_E, clke, and_47_out);
  or or_1 (R0_E, and_5_out, and_9_out);
  or or_2 (R1_E, and_6_out, and_10_out);
  or or_3 (R2_E, and_7_out, and_11_out);
  or or_4 (R3_E, and_8_out, and_12_out);
  and and_5 (and_5_out, clke, or_9_out, cpu_decoder_2x4_west_1__0);
  and and_6 (and_6_out, clke, or_9_out, cpu_decoder_2x4_west_1__1);
  and and_7 (and_7_out, clke, or_9_out, cpu_decoder_2x4_west_1__2);
  and and_8 (and_8_out, clke, or_9_out, cpu_decoder_2x4_west_1__3);
  and and_9 (and_9_out, clke, or_10_out, cpu_decoder_2x4_west_2__0);
  and and_10 (and_10_out, clke, or_10_out, cpu_decoder_2x4_west_2__1);
  and and_11 (and_11_out, clke, or_10_out, cpu_decoder_2x4_west_2__2);
  and and_12 (and_12_out, clke, or_10_out, cpu_decoder_2x4_west_2__3);
  or or_5 (BUS_1, and_17_out, and_38_out, and_37_out, and_34_out);
  or or_6 (or_6_out, and_17_out, and_34_out, and_36_out, and_37_out);
  or or_7 (or_7_out, cpu_stepper_1_step_2, and_50_out, and_45_out, and_44_out, and_42_out);
  or or_8 (or_8_out, cpu_stepper_1_step_3, and_46_out, and_49_out, and_48_out);
  and and_13 (ALU_0, cpu_stepper_1_step_5, IR_IN[7], IR_IN[4]);
  and and_14 (ALU_1, cpu_stepper_1_step_5, IR_IN[7], IR_IN[5]);
  and and_15 (ALU_2, cpu_stepper_1_step_5, IR_IN[7], IR_IN[6]);
  not not_1 (not_1_out, LOAD);
  not not_2 (not_2_out, LOAD);
  and and_16 (and_16_out, clk, not_1_out);
  and and_17 (and_17_out, not_2_out, cpu_stepper_1_step_1);
  CPU_DECODER_2x4_WEST cpu_decoder_2x4_west_1 (
    .a(IR_IN[0]), .b(IR_IN[1]), ._0(cpu_decoder_2x4_west_1__0), ._1(cpu_decoder_2x4_west_1__1),
    ._2(cpu_decoder_2x4_west_1__2), ._3(cpu_decoder_2x4_west_1__3));
  CPU_DECODER_2x4_WEST cpu_decoder_2x4_west_2 (
    .a(IR_IN[2]), .b(IR_IN[3]), ._0(cpu_decoder_2x4_west_2__0), ._1(cpu_decoder_2x4_west_2__1),
    ._2(cpu_decoder_2x4_west_2__2), ._3(cpu_decoder_2x4_west_2__3));
  or or_9 (or_9_out, and_31_out, and_43_out, and_35_out, and_39_out);
  or or_10 (or_10_out, and_33_out, and_32_out, C_2);
  CPU_DECODER_CTRL_3x8 cpu_decoder_ctrl_3x8_1 (
    ._0(cpu_decoder_ctrl_3x8_1__0), ._1(cpu_decoder_ctrl_3x8_1__1), ._2(cpu_decoder_ctrl_3x8_1__2),
    ._3(cpu_decoder_ctrl_3x8_1__3), ._4(cpu_decoder_ctrl_3x8_1__4), ._5(cpu_decoder_ctrl_3x8_1__5),
    ._6(cpu_decoder_ctrl_3x8_1__6), ._7(cpu_decoder_ctrl_3x8_1__7), .c(IR_IN[6]), .b(IR_IN[5]), .a(IR_IN[4]));
  not not_3 (not_3_out, IR_IN[7]);
  and and_18 (and_18_out, not_3_out, cpu_decoder_ctrl_3x8_1__0);
  and and_19 (and_19_out, not_3_out, cpu_decoder_ctrl_3x8_1__1);
  and and_20 (and_20_out, not_3_out, cpu_decoder_ctrl_3x8_1__2);
  and and_21 (and_21_out, not_3_out, cpu_decoder_ctrl_3x8_1__3);
  and and_22 (and_22_out, not_3_out, cpu_decoder_ctrl_3x8_1__4);
  and and_23 (and_23_out, not_3_out, cpu_decoder_ctrl_3x8_1__5);
  and and_24 (and_24_out, not_3_out, cpu_decoder_ctrl_3x8_1__6);
  and and_25 (and_25_out, not_3_out, cpu_decoder_ctrl_3x8_1__7);
  not not_4 (not_4_out, IR_IN[5]);
  not not_5 (not_5_out, IR_IN[4]);
  not not_6 (not_6_out, and_26_out);
  and and_26 (and_26_out, IR_IN[4], IR_IN[5], IR_IN[6]);
  and and_27 (and_27_out, C, IR_IN[3]);
  and and_28 (and_28_out, A, IR_IN[2]);
  and and_29 (and_29_out, E, IR_IN[1]);
  and and_30 (and_30_out, Z, IR_IN[0]);
  and and_31 (and_31_out, cpu_stepper_1_step_4, IR_IN[7]);
  and and_32 (and_32_out, cpu_stepper_1_step_4, and_18_out);
  and and_33 (and_33_out, cpu_stepper_1_step_4, and_19_out);
  and and_34 (and_34_out, cpu_stepper_1_step_4, and_20_out);
  and and_35 (and_35_out, cpu_stepper_1_step_4, and_21_out);
  and and_36 (and_36_out, cpu_stepper_1_step_4, and_22_out);
  and and_37 (and_37_out, cpu_stepper_1_step_4, and_23_out);
  and and_38 (and_38_out, cpu_stepper_1_step_4, and_24_out);
  and and_39 (and_39_out, cpu_stepper_1_step_4, and_25_out, IR_IN[3]);
  and and_40 (END, IR_IN[7], IR_IN[6], not_4_out, not_5_out, cpu_stepper_1_step_4, IR_IN[3], IR_IN[2], IR_IN[1], IR_IN[0]);
  or or_11 (or_11_out, and_27_out, and_28_out, and_29_out, and_30_out);
  CPU_STEPPER cpu_stepper_1 (
    .reset(cpu_stepper_1_step_7), .clk(and_16_out), .step_1(cpu_stepper_1_step_1),
    .step_2(cpu_stepper_1_step_2), .step_3(cpu_stepper_1_step_3), .step_4(cpu_stepper_1_step_4),
    .step_5(cpu_stepper_1_step_5), .step_6(cpu_stepper_1_step_6), .step_7(cpu_stepper_1_step_7));
  and and_41 (C_2, cpu_stepper_1_step_5, IR_IN[7]);
  and and_42 (and_42_out, cpu_stepper_1_step_5, and_18_out);
  and and_43 (and_43_out, cpu_stepper_1_step_5, and_19_out);
  and and_44 (and_44_out, cpu_stepper_1_step_5, and_20_out);
  and and_45 (and_45_out, cpu_stepper_1_step_5, and_22_out);
  and and_46 (and_46_out, cpu_stepper_1_step_5, and_23_out);
  and and_47 (and_47_out, cpu_stepper_1_step_5, and_25_out, not_7_out);
  not not_7 (not_7_out, IR_IN[3]);
  and and_48 (and_48_out, cpu_stepper_1_step_6, IR_IN[7], not_6_out);
  and and_49 (and_49_out, cpu_stepper_1_step_6, and_20_out);
  and and_50 (and_50_out, cpu_stepper_1_step_6, and_23_out, or_11_out);
  CPU_DECODER_2x4 cpu_decoder_2x4_1 (
    .a(IR_IN[0]), .b(IR_IN[1]), ._0(cpu_decoder_2x4_1__0), ._1(cpu_decoder_2x4_1__1),
    ._2(cpu_decoder_2x4_1__2), ._3(cpu_decoder_2x4_1__3));
  or or_12 (or_12_out, and_17_out, and_34_out, and_37_out, and_32_out, and_33_out, and_36_out);
  or or_13 (or_13_out, cpu_stepper_1_step_3, and_35_out, and_46_out, and_45_out, and_49_out, and_50_out);
  or or_14 (or_14_out, and_17_out, and_34_out, and_37_out, C_2);
  or or_15 (or_15_out, and_38_out, C_2);
  or or_16 (or_16_out, and_42_out, and_48_out, and_44_out, and_47_out);
  and and_51 (and_51_out, clks, cpu_stepper_1_step_2);
  or or_17 (or_17_out, MARS, in_5);
  and and_52 (and_52_out, clks, or_12_out);
  and and_53 (and_53_out, clks, or_13_out);
  and and_54 (and_54_out, clks, or_14_out);
  and and_55 (and_55_out, LOAD, clks);
  and and_56 (and_56_out, clks, and_43_out);
  and and_57 (and_57_out, clks, and_31_out);
  and and_58 (and_58_out, clks, or_15_out);
  and and_59 (IO_CLK_S, clks, and_39_out);
  and and_60 (and_60_out, clks, or_16_out, cpu_decoder_2x4_1__0);
  and and_61 (and_61_out, clks, or_16_out, cpu_decoder_2x4_1__1);
  and and_62 (and_62_out, clks, or_16_out, cpu_decoder_2x4_1__2);
  and and_63 (and_63_out, clks, or_16_out, cpu_decoder_2x4_1__3);
  or or_18 (IR_S, in_5, and_51_out);
  or or_19 (MAR_S, or_17_out, and_52_out);
  or or_20 (IAR_S, in_5, and_53_out);
  or or_21 (ACC_S, in_5, and_54_out);
  or or_22 (RAM_S, and_55_out, and_56_out);
  or or_23 (TMP_S, in_5, and_57_out);
  or or_24 (FLAG_S, in_5, and_58_out);
  or or_25 (R0_S, in_5, and_60_out);
  or or_26 (R1_S, in_5, and_61_out);
  or or_27 (R2_S, in_5, and_62_out);
  or or_28 (R3_S, in_5, and_63_out);

  assign DA = IR_IN[3];
  assign IO = IR_IN[2];

  // Notes on the sheet:
  //   REG B_E
  //   REG A
  //   REG B_S
endmodule

module CPU_BUS_1 (
  input  [7:0] i,
  input  bus_1,
  output [7:0] o
);

  wire not_1_out;

  and and_1 (o[6], i[6], not_1_out);
  and and_2 (o[7], i[7], not_1_out);
  and and_3 (o[4], i[4], not_1_out);
  and and_4 (o[5], i[5], not_1_out);
  and and_5 (o[2], i[2], not_1_out);
  and and_6 (o[3], i[3], not_1_out);
  or or_1 (o[0], i[0], bus_1);
  and and_7 (o[1], i[1], not_1_out);
  not not_1 (not_1_out, bus_1);
endmodule

module CPU_DECODER_4x16 (
  input  [3:0] in_1,
  output L,
  output out_3,
  output out_4,
  output out_5,
  output out_6,
  output out_7,
  output out_8,
  output out_9,
  output out_10,
  output out_11,
  output out_12,
  output out_13,
  output out_14,
  output out_15,
  output out_16,
  output M
);

  wire not_1_out, not_2_out, not_3_out, not_4_out;

  not not_1 (not_1_out, in_1[0]);
  not not_2 (not_2_out, in_1[1]);
  not not_3 (not_3_out, in_1[2]);
  not not_4 (not_4_out, in_1[3]);
  and and_1 (L, not_4_out, not_3_out, not_2_out, not_1_out);
  and and_2 (out_3, not_4_out, not_3_out, not_2_out, in_1[0]);
  and and_3 (out_4, not_4_out, not_3_out, in_1[1], not_1_out);
  and and_4 (out_5, not_4_out, not_3_out, in_1[1], in_1[0]);
  and and_5 (out_6, not_4_out, in_1[2], not_2_out, not_1_out);
  and and_6 (out_7, not_4_out, in_1[2], not_2_out, in_1[0]);
  and and_7 (out_8, not_4_out, in_1[2], in_1[1], not_1_out);
  and and_8 (out_9, not_4_out, in_1[2], in_1[1], in_1[0]);
  and and_9 (out_10, in_1[3], not_3_out, not_2_out, not_1_out);
  and and_10 (out_11, in_1[3], not_3_out, not_2_out, in_1[0]);
  and and_11 (out_12, in_1[3], not_3_out, in_1[1], not_1_out);
  and and_12 (out_13, in_1[3], not_3_out, in_1[1], in_1[0]);
  and and_13 (out_14, in_1[3], in_1[2], not_2_out, not_1_out);
  and and_14 (out_15, in_1[3], in_1[2], not_2_out, in_1[0]);
  and and_15 (out_16, in_1[3], in_1[2], in_1[1], not_1_out);
  and and_16 (M, in_1[3], in_1[2], in_1[1], in_1[0]);
endmodule

module CPU_REG_BYTE (
  input  [7:0] i,
  input  RESET,
  input  h,
  input  v,
  input  s,
  input  e,
  output [7:0] o,
  output [7:0] op
);

  wire and_1_out, and_2_out, and_3_out, or_1_out;
  wire [7:0] cpu_reg_8_1_o;

  and and_1 (and_1_out, h, v);
  and and_2 (and_2_out, and_1_out, s);
  and and_3 (and_3_out, and_1_out, e);
  CPU_REG_8 cpu_reg_8_1 (.i(i), .s(or_1_out), .e(and_3_out), .REG(op), .o(cpu_reg_8_1_o));
  or or_1 (or_1_out, RESET, and_2_out);
  assign o = and_3_out ? cpu_reg_8_1_o : 8'bz;  // Controlled_Buffer controlled_buffer_1
endmodule

module CPU_RAM_256 (
  input  reset,
  input  sa,
  input  [7:0] i,
  input  [7:0] address,
  input  s,
  input  e,
  output [7:0] o,
  output [7:0] _15,
  output [7:0] _14,
  output [7:0] _13,
  output [7:0] _12,
  output [7:0] _11,
  output [7:0] _10,
  output [7:0] _9,
  output [7:0] _8,
  output [7:0] _7,
  output [7:0] _6,
  output [7:0] _5,
  output [7:0] _4,
  output [7:0] _3,
  output [7:0] _2,
  output [7:0] _1,
  output [7:0] _0,
  output [7:0] _31,
  output [7:0] _30,
  output [7:0] _29,
  output [7:0] _28,
  output [7:0] _27,
  output [7:0] _26,
  output [7:0] _25,
  output [7:0] _24,
  output [7:0] _23,
  output [7:0] _22,
  output [7:0] _21,
  output [7:0] _20,
  output [7:0] _19,
  output [7:0] _18,
  output [7:0] _17,
  output [7:0] _16,
  output [7:0] _47,
  output [7:0] _46,
  output [7:0] _45,
  output [7:0] _44,
  output [7:0] _43,
  output [7:0] _42,
  output [7:0] _41,
  output [7:0] _40,
  output [7:0] _39,
  output [7:0] _38,
  output [7:0] _37,
  output [7:0] _36,
  output [7:0] _35,
  output [7:0] _34,
  output [7:0] _33,
  output [7:0] _32,
  output [7:0] _63,
  output [7:0] _62,
  output [7:0] _61,
  output [7:0] _60,
  output [7:0] _59,
  output [7:0] _58,
  output [7:0] _57,
  output [7:0] _56,
  output [7:0] _55,
  output [7:0] _54,
  output [7:0] _53,
  output [7:0] _52,
  output [7:0] _51,
  output [7:0] _50,
  output [7:0] _49,
  output [7:0] _48,
  output [7:0] _79,
  output [7:0] _78,
  output [7:0] _77,
  output [7:0] _76,
  output [7:0] _75,
  output [7:0] _74,
  output [7:0] _73,
  output [7:0] _72,
  output [7:0] _71,
  output [7:0] _70,
  output [7:0] _69,
  output [7:0] _68,
  output [7:0] _67,
  output [7:0] _65,
  output [7:0] _65_2,
  output [7:0] _64,
  output [7:0] _95,
  output [7:0] _94,
  output [7:0] _93,
  output [7:0] _92,
  output [7:0] _91,
  output [7:0] _90,
  output [7:0] _89,
  output [7:0] _88,
  output [7:0] _87,
  output [7:0] _86,
  output [7:0] _85,
  output [7:0] _84,
  output [7:0] _83,
  output [7:0] _82,
  output [7:0] _81,
  output [7:0] _80,
  output [7:0] _111,
  output [7:0] _110,
  output [7:0] _109,
  output [7:0] _108,
  output [7:0] _107,
  output [7:0] _106,
  output [7:0] _105,
  output [7:0] _104,
  output [7:0] _103,
  output [7:0] _102,
  output [7:0] _101,
  output [7:0] _100,
  output [7:0] _99,
  output [7:0] _98,
  output [7:0] _97,
  output [7:0] _96,
  output [7:0] _127,
  output [7:0] _126,
  output [7:0] _125,
  output [7:0] _124,
  output [7:0] _123,
  output [7:0] _122,
  output [7:0] _121,
  output [7:0] _120,
  output [7:0] _119,
  output [7:0] _118,
  output [7:0] _117,
  output [7:0] _116,
  output [7:0] _115,
  output [7:0] _114,
  output [7:0] _113,
  output [7:0] _112,
  output [7:0] _143,
  output [7:0] _142,
  output [7:0] _141,
  output [7:0] _140,
  output [7:0] _139,
  output [7:0] _138,
  output [7:0] _137,
  output [7:0] _136,
  output [7:0] _135,
  output [7:0] _134,
  output [7:0] _133,
  output [7:0] _132,
  output [7:0] _131,
  output [7:0] _130,
  output [7:0] _129,
  output [7:0] _128,
  output [7:0] _159,
  output [7:0] _158,
  output [7:0] _157,
  output [7:0] _156,
  output [7:0] _155,
  output [7:0] _154,
  output [7:0] _153,
  output [7:0] _152,
  output [7:0] _151,
  output [7:0] _150,
  output [7:0] _149,
  output [7:0] _148,
  output [7:0] _147,
  output [7:0] _146,
  output [7:0] _145,
  output [7:0] _144,
  output [7:0] _175,
  output [7:0] _174,
  output [7:0] _173,
  output [7:0] _172,
  output [7:0] _171,
  output [7:0] _170,
  output [7:0] _169,
  output [7:0] _168,
  output [7:0] _167,
  output [7:0] _166,
  output [7:0] _165,
  output [7:0] _164,
  output [7:0] _163,
  output [7:0] _162,
  output [7:0] _161,
  output [7:0] _160,
  output [7:0] _191,
  output [7:0] _190,
  output [7:0] _189,
  output [7:0] _188,
  output [7:0] _187,
  output [7:0] _186,
  output [7:0] _185,
  output [7:0] _184,
  output [7:0] _183,
  output [7:0] _182,
  output [7:0] _181,
  output [7:0] _180,
  output [7:0] _179,
  output [7:0] _178,
  output [7:0] _177,
  output [7:0] _176,
  output [7:0] _207,
  output [7:0] _206,
  output [7:0] _205,
  output [7:0] _204,
  output [7:0] _203,
  output [7:0] _202,
  output [7:0] _201,
  output [7:0] _200,
  output [7:0] _199,
  output [7:0] _198,
  output [7:0] _197,
  output [7:0] _196,
  output [7:0] _195,
  output [7:0] _194,
  output [7:0] _193,
  output [7:0] _192,
  output [7:0] _223,
  output [7:0] _222,
  output [7:0] _221,
  output [7:0] _220,
  output [7:0] _219,
  output [7:0] _218,
  output [7:0] _217,
  output [7:0] _216,
  output [7:0] _215,
  output [7:0] _214,
  output [7:0] _213,
  output [7:0] _212,
  output [7:0] _211,
  output [7:0] _210,
  output [7:0] _209,
  output [7:0] _208,
  output [7:0] _239,
  output [7:0] _238,
  output [7:0] _237,
  output [7:0] _236,
  output [7:0] _235,
  output [7:0] _234,
  output [7:0] _233,
  output [7:0] _232,
  output [7:0] _231,
  output [7:0] _230,
  output [7:0] _229,
  output [7:0] _228,
  output [7:0] _227,
  output [7:0] _226,
  output [7:0] _225,
  output [7:0] _224,
  output [7:0] _255,
  output [7:0] _254,
  output [7:0] _253,
  output [7:0] _252,
  output [7:0] _251,
  output [7:0] _250,
  output [7:0] _249,
  output [7:0] _248,
  output [7:0] _247,
  output [7:0] _246,
  output [7:0] _245,
  output [7:0] _244,
  output [7:0] _243,
  output [7:0] _242,
  output [7:0] _241,
  output [7:0] _240
);

  wire cpu_decoder_4x16_1_l, cpu_decoder_4x16_1_m, cpu_decoder_4x16_1_out_3, cpu_decoder_4x16_1_out_4,
       cpu_decoder_4x16_1_out_5, cpu_decoder_4x16_1_out_6, cpu_decoder_4x16_1_out_7,
       cpu_decoder_4x16_1_out_8, cpu_decoder_4x16_1_out_9, cpu_decoder_4x16_1_out_10,
       cpu_decoder_4x16_1_out_11, cpu_decoder_4x16_1_out_12, cpu_decoder_4x16_1_out_13,
       cpu_decoder_4x16_1_out_14, cpu_decoder_4x16_1_out_15, cpu_decoder_4x16_1_out_16, cpu_decoder_4x16_2_l,
       cpu_decoder_4x16_2_m, cpu_decoder_4x16_2_out_3, cpu_decoder_4x16_2_out_4, cpu_decoder_4x16_2_out_5,
       cpu_decoder_4x16_2_out_6, cpu_decoder_4x16_2_out_7, cpu_decoder_4x16_2_out_8,
       cpu_decoder_4x16_2_out_9, cpu_decoder_4x16_2_out_10, cpu_decoder_4x16_2_out_11,
       cpu_decoder_4x16_2_out_12, cpu_decoder_4x16_2_out_13, cpu_decoder_4x16_2_out_14,
       cpu_decoder_4x16_2_out_15, cpu_decoder_4x16_2_out_16;
  wire [3:0] cpu_mem_8_1_o_2;
  wire [7:0] cpu_reg_byte_1_o;
  wire [7:4] cpu_mem_8_1_o;

  CPU_MEM_8 cpu_mem_8_1 (.o({cpu_mem_8_1_o, cpu_mem_8_1_o_2}), .i(address), .e(sa));
  CPU_DECODER_4x16 cpu_decoder_4x16_1 (
    .in_1(cpu_mem_8_1_o), .L(cpu_decoder_4x16_1_l), .out_3(cpu_decoder_4x16_1_out_3),
    .out_4(cpu_decoder_4x16_1_out_4), .out_5(cpu_decoder_4x16_1_out_5), .out_6(cpu_decoder_4x16_1_out_6),
    .out_7(cpu_decoder_4x16_1_out_7), .out_8(cpu_decoder_4x16_1_out_8), .out_9(cpu_decoder_4x16_1_out_9),
    .out_10(cpu_decoder_4x16_1_out_10), .out_11(cpu_decoder_4x16_1_out_11),
    .out_12(cpu_decoder_4x16_1_out_12), .out_13(cpu_decoder_4x16_1_out_13),
    .out_14(cpu_decoder_4x16_1_out_14), .out_15(cpu_decoder_4x16_1_out_15),
    .out_16(cpu_decoder_4x16_1_out_16), .M(cpu_decoder_4x16_1_m));
  assign o = e ? cpu_reg_byte_1_o : 8'bz;  // Controlled_Buffer controlled_buffer_1
  CPU_REG_BYTE cpu_reg_byte_1 (
    .op(_15), .RESET(reset), .h(cpu_decoder_4x16_1_l), .v(cpu_decoder_4x16_2_m), .i(i), .o(cpu_reg_byte_1_o),
    .s(s), .e(e));
  CPU_REG_BYTE cpu_reg_byte_2 (
    .op(_31), .RESET(reset), .h(cpu_decoder_4x16_1_out_3), .v(cpu_decoder_4x16_2_m), .i(i),
    .o(cpu_reg_byte_1_o), .s(s), .e(e));
  CPU_REG_BYTE cpu_reg_byte_3 (
    .op(_14), .RESET(reset), .h(cpu_decoder_4x16_1_l), .v(cpu_decoder_4x16_2_out_16), .i(i),
    .o(cpu_reg_byte_1_o), .s(s), .e(e));
  CPU_REG_BYTE cpu_reg_byte_4 (
    .op(_30), .RESET(reset), .h(cpu_decoder_4x16_1_out_3), .v(cpu_decoder_4x16_2_out_16), .i(i),
    .o(cpu_reg_byte_1_o), .s(s), .e(e));
  CPU_REG_BYTE cpu_reg_byte_5 (
    .op(_13), .RESET(reset), .h(cpu_decoder_4x16_1_l), .v(cpu_decoder_4x16_2_out_15), .i(i),
    .o(cpu_reg_byte_1_o), .s(s), .e(e));
  CPU_REG_BYTE cpu_reg_byte_6 (
    .op(_29), .RESET(reset), .h(cpu_decoder_4x16_1_out_3), .v(cpu_decoder_4x16_2_out_15), .i(i),
    .o(cpu_reg_byte_1_o), .s(s), .e(e));
  CPU_REG_BYTE cpu_reg_byte_7 (
    .op(_12), .RESET(reset), .h(cpu_decoder_4x16_1_l), .v(cpu_decoder_4x16_2_out_14), .i(i),
    .o(cpu_reg_byte_1_o), .s(s), .e(e));
  CPU_REG_BYTE cpu_reg_byte_8 (
    .op(_28), .RESET(reset), .h(cpu_decoder_4x16_1_out_3), .v(cpu_decoder_4x16_2_out_14), .i(i),
    .o(cpu_reg_byte_1_o), .s(s), .e(e));
  CPU_REG_BYTE cpu_reg_byte_9 (
    .op(_11), .RESET(reset), .h(cpu_decoder_4x16_1_l), .v(cpu_decoder_4x16_2_out_13), .i(i),
    .o(cpu_reg_byte_1_o), .s(s), .e(e));
  CPU_REG_BYTE cpu_reg_byte_10 (
    .op(_27), .RESET(reset), .h(cpu_decoder_4x16_1_out_3), .v(cpu_decoder_4x16_2_out_13), .i(i),
    .o(cpu_reg_byte_1_o), .s(s), .e(e));
  CPU_REG_BYTE cpu_reg_byte_11 (
    .op(_10), .RESET(reset), .h(cpu_decoder_4x16_1_l), .v(cpu_decoder_4x16_2_out_12), .i(i),
    .o(cpu_reg_byte_1_o), .s(s), .e(e));
  CPU_REG_BYTE cpu_reg_byte_12 (
    .op(_26), .RESET(reset), .h(cpu_decoder_4x16_1_out_3), .v(cpu_decoder_4x16_2_out_12), .i(i),
    .o(cpu_reg_byte_1_o), .s(s), .e(e));
  CPU_REG_BYTE cpu_reg_byte_13 (
    .op(_9), .RESET(reset), .h(cpu_decoder_4x16_1_l), .v(cpu_decoder_4x16_2_out_11), .i(i),
    .o(cpu_reg_byte_1_o), .s(s), .e(e));
  CPU_REG_BYTE cpu_reg_byte_14 (
    .op(_25), .RESET(reset), .h(cpu_decoder_4x16_1_out_3), .v(cpu_decoder_4x16_2_out_11), .i(i),
    .o(cpu_reg_byte_1_o), .s(s), .e(e));
  CPU_REG_BYTE cpu_reg_byte_15 (
    .op(_8), .RESET(reset), .h(cpu_decoder_4x16_1_l), .v(cpu_decoder_4x16_2_out_10), .i(i),
    .o(cpu_reg_byte_1_o), .s(s), .e(e));
  CPU_REG_BYTE cpu_reg_byte_16 (
    .op(_24), .RESET(reset), .h(cpu_decoder_4x16_1_out_3), .v(cpu_decoder_4x16_2_out_10), .i(i),
    .o(cpu_reg_byte_1_o), .s(s), .e(e));
  CPU_DECODER_4x16 cpu_decoder_4x16_2 (
    .in_1(cpu_mem_8_1_o_2), .L(cpu_decoder_4x16_2_l), .out_3(cpu_decoder_4x16_2_out_3),
    .out_4(cpu_decoder_4x16_2_out_4), .out_5(cpu_decoder_4x16_2_out_5), .out_6(cpu_decoder_4x16_2_out_6),
    .out_7(cpu_decoder_4x16_2_out_7), .out_8(cpu_decoder_4x16_2_out_8), .out_9(cpu_decoder_4x16_2_out_9),
    .out_10(cpu_decoder_4x16_2_out_10), .out_11(cpu_decoder_4x16_2_out_11),
    .out_12(cpu_decoder_4x16_2_out_12), .out_13(cpu_decoder_4x16_2_out_13),
    .out_14(cpu_decoder_4x16_2_out_14), .out_15(cpu_decoder_4x16_2_out_15),
    .out_16(cpu_decoder_4x16_2_out_16), .M(cpu_decoder_4x16_2_m));
  CPU_REG_BYTE cpu_reg_byte_17 (
    .op(_7), .RESET(reset), .h(cpu_decoder_4x16_1_l), .v(cpu_decoder_4x16_2_out_9), .i(i),
    .o(cpu_reg_byte_1_o), .s(s), .e(e));
  CPU_REG_BYTE cpu_reg_byte_18 (
    .op(_23), .RESET(reset), .h(cpu_decoder_4x16_1_out_3), .v(cpu_decoder_4x16_2_out_9), .i(i),
    .o(cpu_reg_byte_1_o), .s(s), .e(e));
  CPU_REG_BYTE cpu_reg_byte_19 (
    .op(_6), .RESET(reset), .h(cpu_decoder_4x16_1_l), .v(cpu_decoder_4x16_2_out_8), .i(i),
    .o(cpu_reg_byte_1_o), .s(s), .e(e));
  CPU_REG_BYTE cpu_reg_byte_20 (
    .op(_22), .RESET(reset), .h(cpu_decoder_4x16_1_out_3), .v(cpu_decoder_4x16_2_out_8), .i(i),
    .o(cpu_reg_byte_1_o), .s(s), .e(e));
  CPU_REG_BYTE cpu_reg_byte_21 (
    .op(_5), .RESET(reset), .h(cpu_decoder_4x16_1_l), .v(cpu_decoder_4x16_2_out_7), .i(i),
    .o(cpu_reg_byte_1_o), .s(s), .e(e));
  CPU_REG_BYTE cpu_reg_byte_22 (
    .op(_21), .RESET(reset), .h(cpu_decoder_4x16_1_out_3), .v(cpu_decoder_4x16_2_out_7), .i(i),
    .o(cpu_reg_byte_1_o), .s(s), .e(e));
  CPU_REG_BYTE cpu_reg_byte_23 (
    .op(_4), .RESET(reset), .h(cpu_decoder_4x16_1_l), .v(cpu_decoder_4x16_2_out_6), .i(i),
    .o(cpu_reg_byte_1_o), .s(s), .e(e));
  CPU_REG_BYTE cpu_reg_byte_24 (
    .op(_20), .RESET(reset), .h(cpu_decoder_4x16_1_out_3), .v(cpu_decoder_4x16_2_out_6), .i(i),
    .o(cpu_reg_byte_1_o), .s(s), .e(e));
  CPU_REG_BYTE cpu_reg_byte_25 (
    .op(_3), .RESET(reset), .h(cpu_decoder_4x16_1_l), .v(cpu_decoder_4x16_2_out_5), .i(i),
    .o(cpu_reg_byte_1_o), .s(s), .e(e));
  CPU_REG_BYTE cpu_reg_byte_26 (
    .op(_19), .RESET(reset), .h(cpu_decoder_4x16_1_out_3), .v(cpu_decoder_4x16_2_out_5), .i(i),
    .o(cpu_reg_byte_1_o), .s(s), .e(e));
  CPU_REG_BYTE cpu_reg_byte_27 (
    .op(_2), .RESET(reset), .h(cpu_decoder_4x16_1_l), .v(cpu_decoder_4x16_2_out_4), .i(i),
    .o(cpu_reg_byte_1_o), .s(s), .e(e));
  CPU_REG_BYTE cpu_reg_byte_28 (
    .op(_18), .RESET(reset), .h(cpu_decoder_4x16_1_out_3), .v(cpu_decoder_4x16_2_out_4), .i(i),
    .o(cpu_reg_byte_1_o), .s(s), .e(e));
  CPU_REG_BYTE cpu_reg_byte_29 (
    .op(_1), .RESET(reset), .h(cpu_decoder_4x16_1_l), .v(cpu_decoder_4x16_2_out_3), .i(i),
    .o(cpu_reg_byte_1_o), .s(s), .e(e));
  CPU_REG_BYTE cpu_reg_byte_30 (
    .op(_17), .RESET(reset), .h(cpu_decoder_4x16_1_out_3), .v(cpu_decoder_4x16_2_out_3), .i(i),
    .o(cpu_reg_byte_1_o), .s(s), .e(e));
  CPU_REG_BYTE cpu_reg_byte_31 (
    .op(_0), .RESET(reset), .h(cpu_decoder_4x16_1_l), .v(cpu_decoder_4x16_2_l), .i(i), .o(cpu_reg_byte_1_o),
    .s(s), .e(e));
  CPU_REG_BYTE cpu_reg_byte_32 (
    .op(_16), .RESET(reset), .h(cpu_decoder_4x16_1_out_3), .v(cpu_decoder_4x16_2_l), .i(i),
    .o(cpu_reg_byte_1_o), .s(s), .e(e));
endmodule

module CPU_CARRY_TEMP (
  input  c,
  input  s,
  output o
);

  CPU_MEM_1 cpu_mem_1_1 (.e(s), .s(c), .q(o));
endmodule

module CPU_DELAY (
  input  [7:0] in_1,
  input  clk,
  output [7:0] out_3
);

  Counter #(.ongoal("stay"), .trigger("falling"), .behavior("old")) counter_1 (
    .load(1'b1), .D(in_1), .count(1'b0), .Q(out_3), .clk(clk));  // open: carry, clr, preset
endmodule

module LOAD_256_COUNT (
  input  clk,
  output [7:0] out_2,
  output carry
);

  wire counter_1_carry;

  Counter #(.ongoal("stay"), .trigger("falling"), .behavior("old")) counter_1 (
    .count(1'b1), .Q(out_2), .carry(counter_1_carry), .clk(clk));  // open: load, D, clr, preset
  not not_1 (carry, counter_1_carry);

  // Notes on the sheet:
  //   count
endmodule

module CPU (
  input  in_1,
  input  in_2,
  input  MARS,
  input  RESET,
  input  [7:0] RAM_INPUT,
  output [7:0] R0,
  output [7:0] R1,
  output [7:0] R1_2,
  output [7:0] R3,
  output out_10,
  output clke,
  output clks,
  output END,
  output S,
  output E,
  output IO,
  output DA,
  output [7:0] out_18,
  output [7:0] out_19,
  output [7:0] out_20,
  output [7:0] BUS_OUTPUT
);

  wire and_1_out, and_2_out, and_3_out, C, cpu_alu_1_a_larger, cpu_alu_1_carry_out, cpu_alu_1_equal,
       cpu_alu_1_zero, cpu_carry_temp_1_o, cpu_control_section_1_acc_e, cpu_control_section_1_acc_s,
       cpu_control_section_1_alu_0, cpu_control_section_1_alu_1, cpu_control_section_1_alu_2,
       cpu_control_section_1_bus_1, cpu_control_section_1_flag_s, cpu_control_section_1_iar_e,
       cpu_control_section_1_iar_s, cpu_control_section_1_ir_s, cpu_control_section_1_mar_s,
       cpu_control_section_1_r0_e, cpu_control_section_1_r0_s, cpu_control_section_1_r1_e,
       cpu_control_section_1_r1_s, cpu_control_section_1_r2_e, cpu_control_section_1_r2_s,
       cpu_control_section_1_r3_e, cpu_control_section_1_r3_s, cpu_control_section_1_ram_e,
       cpu_control_section_1_ram_s, cpu_flags_1_a_2, cpu_flags_1_c_2, cpu_flags_1_e_2, cpu_flags_1_z_2,
       not_1_out, S_t;
  wire [7:0] cpu_alu_1_o, cpu_bus_1_1_o, cpu_ram_256_1__124, cpu_tmp_1_o, load_256_count_1_out_2,
       multiplexer_1_out;

  CPU_ACCUMULATOR cpu_accumulator_1 (
    .i(cpu_alu_1_o), .\reg (out_20), .o(BUS_OUTPUT), .s(cpu_control_section_1_acc_s),
    .e(cpu_control_section_1_acc_e));
  CPU_TMP cpu_tmp_1 (.i(BUS_OUTPUT), .in_2(S_t), .o(cpu_tmp_1_o));
  CPU_BUS_1 cpu_bus_1_1 (.i(cpu_tmp_1_o), .bus_1(cpu_control_section_1_bus_1), .o(cpu_bus_1_1_o));
  CPU_ALU cpu_alu_1 (
    .a_larger(cpu_alu_1_a_larger), .equal(cpu_alu_1_equal), .a(BUS_OUTPUT), .o(cpu_alu_1_o),
    .b(cpu_bus_1_1_o), .carry_out(cpu_alu_1_carry_out), .carry_in(and_2_out),
    .a_2(cpu_control_section_1_alu_0), .b_2(cpu_control_section_1_alu_1), .c(cpu_control_section_1_alu_2),
    .zero(cpu_alu_1_zero));
  not not_1 (not_1_out, END);
  and and_1 (and_1_out, in_1, not_1_out);
  and and_2 (and_2_out, cpu_carry_temp_1_o, C);
  and and_3 (and_3_out, in_2, out_10);
  CPU_CLK cpu_clk_1 (.clkin(and_1_out), .clk(out_10), .clks(clks), .clke(clke));
  CPU_CARRY_TEMP cpu_carry_temp_1 (.c(cpu_flags_1_c_2), .s(S_t), .o(cpu_carry_temp_1_o));
  CPU_FLAGS cpu_flags_1 (
    .C(cpu_alu_1_carry_out), .A(cpu_alu_1_a_larger), .E(cpu_alu_1_equal), .Z(cpu_alu_1_zero),
    .C_2(cpu_flags_1_c_2), .A_2(cpu_flags_1_a_2), .E_2(cpu_flags_1_e_2), .Z_2(cpu_flags_1_z_2),
    .s(cpu_control_section_1_flag_s));
  LOAD_256_COUNT load_256_count_1 (.out_2(load_256_count_1_out_2), .clk(and_3_out));  // open: carry
  assign BUS_OUTPUT = in_2 ? load_256_count_1_out_2 : 8'bz;  // Controlled_Buffer controlled_buffer_1
  CPU_CONTROL_SECTION cpu_control_section_1 (
    .clks(clks), .clk(out_10), .clke(clke), .LOAD(in_2), .MARS(MARS), .in_5(RESET),
    .BUS_1(cpu_control_section_1_bus_1), .IR_S(cpu_control_section_1_ir_s),
    .MAR_S(cpu_control_section_1_mar_s), .IAR_E(cpu_control_section_1_iar_e),
    .IAR_S(cpu_control_section_1_iar_s), .RAM_E(cpu_control_section_1_ram_e),
    .ACC_S(cpu_control_section_1_acc_s), .ACC_E(cpu_control_section_1_acc_e),
    .RAM_S(cpu_control_section_1_ram_s), .C_2(C), .TMP_S(S_t), .IO_CLK_E(E),
    .FLAG_S(cpu_control_section_1_flag_s), .IO_CLK_S(S), .R0_S(cpu_control_section_1_r0_s),
    .R1_S(cpu_control_section_1_r1_s), .R0_E(cpu_control_section_1_r0_e), .R1_E(cpu_control_section_1_r1_e),
    .R2_S(cpu_control_section_1_r2_s), .R2_E(cpu_control_section_1_r2_e), .R3_E(cpu_control_section_1_r3_e),
    .R3_S(cpu_control_section_1_r3_s), .END(END), .IO(IO), .C(cpu_flags_1_c_2), .DA(DA), .A(cpu_flags_1_a_2),
    .E(cpu_flags_1_e_2), .Z(cpu_flags_1_z_2), .ALU_0(cpu_control_section_1_alu_0),
    .ALU_1(cpu_control_section_1_alu_1), .ALU_2(cpu_control_section_1_alu_2), .IR_IN(out_18));
  CPU_R cpu_r_1 (
    .i(BUS_OUTPUT), .\reg (R0), .o(BUS_OUTPUT), .s(cpu_control_section_1_r0_s), .e(cpu_control_section_1_r0_e));
  CPU_R cpu_r_2 (
    .i(BUS_OUTPUT), .\reg (R1), .o(BUS_OUTPUT), .s(cpu_control_section_1_r1_s), .e(cpu_control_section_1_r1_e));
  CPU_IAR cpu_iar_1 (
    .IAR(out_19), .i(BUS_OUTPUT), .o(BUS_OUTPUT), .s(cpu_control_section_1_iar_s),
    .e(cpu_control_section_1_iar_e));
  CPU_IR cpu_ir_1 (.i(BUS_OUTPUT), .o(out_18), .s(cpu_control_section_1_ir_s));
  CPU_R cpu_r_3 (
    .i(BUS_OUTPUT), .\reg (R1_2), .o(BUS_OUTPUT), .s(cpu_control_section_1_r2_s),
    .e(cpu_control_section_1_r2_e));
  CPU_R cpu_r_4 (
    .i(BUS_OUTPUT), .\reg (R3), .o(BUS_OUTPUT), .s(cpu_control_section_1_r3_s), .e(cpu_control_section_1_r3_e));
  Multiplexer #(.width(8)) multiplexer_1 (
    .in0(BUS_OUTPUT), .in1(RAM_INPUT), .out(multiplexer_1_out), .sel(in_2));  // open: en
  CPU_RAM_256 cpu_ram_256_1 (
    .o(BUS_OUTPUT), .reset(RESET), .sa(cpu_control_section_1_mar_s), .i(multiplexer_1_out),
    .address(BUS_OUTPUT), .s(cpu_control_section_1_ram_s), .e(cpu_control_section_1_ram_e),
    ._124(cpu_ram_256_1__124), ._123(cpu_ram_256_1__124));  // open: _15, _14, _13, _12, _11, _10, _9, _8, _7, _6, _5, _4, _3, _2, _1, _0, _31, _30, _29, _28, _27, _26, _25, _24, _23, _22, _21, _20, _19, _18, _17, _16, _47, _46, _45, _44, _43, _42, _41, _40, _39, _38, _37, _36, _35, _34, _33, _32, _63, _62, _61, _60, _59, _58, _57, _56, _55, _54, _53, _52, _51, _50, _49, _48, _79, _78, _77, _76, _75, _74, _73, _72, _71, _70, _69, _68, _67, _65, _65_2, _64, _95, _94, _93, _92, _91, _90, _89, _88, _87, _86, _85, _84, _83, _82, _81, _80, _111, _110, _109, _108, _107, _106, _105, _104, _103, _102, _101, _100, _99, _98, _97, _96, _127, _126, _125, _122, _121, _120, _119, _118, _117, _116, _115, _114, _113, _112, _143, _142, _141, _140, _139, _138, _137, _136, _135, _134, _133, _132, _131, _130, _129, _128, _159, _158, _157, _156, _155, _154, _153, _152, _151, _150, _149, _148, _147, _146, _145, _144, _175, _174, _173, _172, _171, _170, _169, _168, _167, _166, _165, _164, _163, _162, _161, _160, _191, _190, _189, _188, _187, _186, _185, _184, _183, _182, _181, _180, _179, _178, _177, _176, _207, _206, _205, _204, _203, _202, _201, _200, _199, _198, _197, _196, _195, _194, _193, _192, _223, _222, _221, _220, _219, _218, _217, _216, _215, _214, _213, _212, _211, _210, _209, _208, _239, _238, _237, _236, _235, _234, _233, _232, _231, _230, _229, _228, _227, _226, _225, _224, _255, _254, _253, _252, _251, _250, _249, _248, _247, _246, _245, _244, _243, _242, _241, _240

  // Other names for the same wires on the sheet: clkl = out_10; LOAD = in_2

  // Notes on the sheet:
  //   END: pull=up
endmodule

module CPU_TEST (
  input  in_1,
  input  in_2
);

  wire CLK, CLKE, CLKL, CLKS, END, RESET;
  wire [7:0] ACC, BUS, IAR, IR, load_256_count_1_out_2, R0, R1, R2, R3, RAM_INPUT;

  Hex_Digit_Display hex_digit_display_1 (.value(BUS[7:4]));  // open: dp
  Hex_Digit_Display hex_digit_display_2 (.value(BUS[3:0]));  // open: dp
  Hex_Digit_Display hex_digit_display_3 (.value(ACC[7:4]));  // open: dp
  Hex_Digit_Display hex_digit_display_4 (.value(ACC[3:0]));  // open: dp
  LOAD_256_COUNT load_256_count_1 (.out_2(load_256_count_1_out_2), .clk(CLKL));  // open: carry
  Hex_Digit_Display hex_digit_display_5 (.value(IAR[3:0]));  // open: dp
  Hex_Digit_Display hex_digit_display_6 (.value(IAR[7:4]));  // open: dp
  Hex_Digit_Display hex_digit_display_7 (.value(IR[7:4]));  // open: dp
  RAM #(.Select("high"), .simpleMode("false")) ram_1 (
    .addr(load_256_count_1_out_2), .data(RAM_INPUT), .sel(in_1), .clk(CLKL), .ld(1'b1), .clr(1'b0));
  Hex_Digit_Display hex_digit_display_8 (.value(IR[3:0]));  // open: dp
  CPU cpu_1 (
    .in_1(CLK), .out_10(CLKL), .in_2(in_1), .clke(CLKE), .clks(CLKS), .MARS(in_2), .END(END), .RESET(RESET),
    .RAM_INPUT(RAM_INPUT), .BUS_OUTPUT(BUS), .R0(R0), .R1(R1), .R1_2(R2), .R3(R3), .out_19(IAR), .out_18(IR),
    .out_20(ACC));  // open: S, E, IO, DA
  Hex_Digit_Display hex_digit_display_9 (.value(R0[7:4]));  // open: dp
  Hex_Digit_Display hex_digit_display_10 (.value(R0[3:0]));  // open: dp
  Hex_Digit_Display hex_digit_display_11 (.value(R1[7:4]));  // open: dp
  Hex_Digit_Display hex_digit_display_12 (.value(R1[3:0]));  // open: dp
  Hex_Digit_Display hex_digit_display_13 (.value(R2[7:4]));  // open: dp
  Button button_1 (.out(RESET));
  LED led_1 (.in(END));
  Clock clock_1 (.out(CLK));
  Hex_Digit_Display hex_digit_display_14 (.value(R2[3:0]));  // open: dp
  Hex_Digit_Display hex_digit_display_15 (.value(R3[3:0]));  // open: dp
  Hex_Digit_Display hex_digit_display_16 (.value(R3[7:4]));  // open: dp

  // Other names for the same wires on the sheet: LOAD = in_1; MARS = in_2

  // Notes on the sheet:
  //   EXTERNAL RAM
  //   $
  //   1.
  //   2.
  //   3.
  //   0
  //   1
  //   0
endmodule
